// Digital circuit io.dig as structural Verilog
module io (
  input  [7:0] DATA,
  input  [2:0] IO_SEL,
  input  IO_OE,
  input  IO_CP,
  input  IO_AVAIL_OE,
  input  IO0_AVAIL,
  input  IO1_AVAIL,
  input  IO2_AVAIL,
  output IO_AVAIL,
  output IO0_CP,
  output IO0_OE,
  output IO1_CP,
  output IO1_OE,
  output IO2_CP,
  output IO2_OE
);

  _74238 _74238_1 (
    .pin1(IO_SEL[0]), .pin2(IO_SEL[1]), .pin3(IO_SEL[2]), .pin4(1'b0), .pin5(1'b0), .pin6(IO_CP),
    .pin8(1'b0), .pin13(IO2_CP), .pin14(IO1_CP), .pin15(IO0_CP), .pin16(1'b1));  // open: pin7, pin9, pin10, pin11, pin12
  _74138 _74138_1 (
    .pin1(IO_SEL[0]), .pin2(IO_SEL[1]), .pin3(IO_SEL[2]), .pin4(IO_OE), .pin5(1'b0), .pin6(1'b1),
    .pin8(1'b0), .pin13(IO2_OE), .pin14(IO1_OE), .pin15(IO0_OE), .pin16(1'b1));  // open: pin7, pin9, pin10, pin11, pin12
  _74541 _74541_1 (
    .pin1(IO_AVAIL_OE), .pin2(IO0_AVAIL), .pin3(IO1_AVAIL), .pin4(IO2_AVAIL), .pin5(1'b0), .pin6(1'b0),
    .pin7(1'b0), .pin8(1'b0), .pin9(1'b0), .pin10(1'b0), .pin11(DATA[7]), .pin12(DATA[6]), .pin13(DATA[5]),
    .pin14(DATA[4]), .pin15(DATA[3]), .pin16(DATA[2]), .pin17(DATA[1]), .pin18(DATA[0]), .pin19(1'b0),
    .pin20(1'b1));
  or or_1 (IO_AVAIL, IO0_AVAIL, IO1_AVAIL);

  // Notes on the sheet:
  //   IO_OE: default 1
  //   IO_AVAIL_OE: default 1
endmodule

/* Test case io:
IO_OE_ DATA_out
1      Z
*/
