// Digital circuit lcd.dig as structural Verilog
module lcd (
  input  clk,
  input  [7:0] DB,
  input  E,
  input  RW,
  input  RS
);

  wire u_lcd_driver_pix_clk, u_lcd_driver_pix_val;
  wire [1:0] u_lcd_driver_probe_pix_state, u_lcd_driver_probe_state, u_lcd_driver_proble_charrow;
  wire [3:0] u_lcd_driver_probe_pixcol, u_lcd_driver_probe_pixrow;
  wire [4:0] CGROM_d, u_lcd_driver_probe_charcol;
  wire [6:0] u_lcd_driver_probe_ac;
  wire [7:0] u_lcd_driver_db_out;
  wire [10:0] u_lcd_driver_cgrom_addr;
  wire [12:0] u_lcd_driver_pix_addr;

  lcd_driver #(.applicationType("GHDL"), .CodeFile("lcd_driver.vhdl")) u_lcd_driver (
    .clk(clk), .en(E), .rw(RW), .rs(RS), .db_in(DB), .cgrom_data(CGROM_d), .db_out(u_lcd_driver_db_out),
    .cgrom_addr(u_lcd_driver_cgrom_addr), .pix_addr(u_lcd_driver_pix_addr), .pix_val(u_lcd_driver_pix_val),
    .pix_clk(u_lcd_driver_pix_clk), .probe_state(u_lcd_driver_probe_state),
    .probe_pix_state(u_lcd_driver_probe_pix_state), .probe_PixRow(u_lcd_driver_probe_pixrow),
    .probe_PixCol(u_lcd_driver_probe_pixcol), .probe_AC(u_lcd_driver_probe_ac),
    .probe_CharCol(u_lcd_driver_probe_charcol), .proble_CharRow(u_lcd_driver_proble_charrow));
  ROM #(.AddrBits(11), .Bits(5)) CGROM (.A(u_lcd_driver_cgrom_addr), .sel(1'b1), .D(CGROM_d));
  // Probe on u_lcd_driver_db_out
  // Probe on u_lcd_driver_probe_state
  // Probe on u_lcd_driver_probe_pix_state
  // Probe on u_lcd_driver_probe_pixrow
  // Probe on u_lcd_driver_probe_pixcol
  // Probe on u_lcd_driver_probe_ac
  // Probe on u_lcd_driver_probe_charcol
  // Probe on u_lcd_driver_proble_charrow
  Break break_1 (.brk(u_lcd_driver_pix_clk));
  GraphicCard #(.graphicHeight(32), .graphicWidth(120)) graphiccard_1 (
    .A(u_lcd_driver_pix_addr), .str(1'b1), .C(u_lcd_driver_pix_clk), .ld(1'b0), .B(1'b0),
    .D(u_lcd_driver_pix_val));

  // Notes on the sheet:
  //   clk: Hz: 2
  //   DB: default 48
  //   RS: default 1
  //   HD44780U
  //   AMC2004A
  //   contents of CGROM (hex, n*v repeats v):
  //   330*0,4*4,0,0,4,0,0,0,a,a,a,7*0,a,a,1f,a,1f,a,a,0,0,0,4,f,14,e
  //   ,5,1e,4,0,0,0,18,19,2,4,8,13,3,0,0,0,c,12,14,8,15,12,d,0,0,0,c
  //   ,4,8,7*0,2,4,8,8,8,4,2,0,0,0,8,4,2,2,2,4,8,4*0,4,15,e,15,4,5*0
  //   ,4,4,1f,4,4,8*0,c,4,8,6*0,1f,11*0,c,c,4*0,1,2,4,8,10,4*0,e,11
  //   ,13,15,19,11,e,0,0,0,4,c,4*4,e,0,0,0,e,11,1,2,4,8,1f,0,0,0,1f
  //   ,2,4,2,1,11,e,0,0,0,2,6,a,12,1f,2,2,0,0,0,1f,10,1e,1,1,11,e,0,0,0
  //   ,6,8,10,1e,11,11,e,0,0,0,1f,11,1,2,4,4,4,0,0,0,e,11,11,e,11,11
  //   ,e,0,0,0,e,11,11,f,1,2,c,4*0,c,c,0,c,c,5*0,c,c,0,c,4,8,0,0,0,2
  //   ,4,8,10,8,4,2,5*0,1f,0,1f,5*0,8,4,2,1,2,4,8,0,0,0,e,11,1,2,4,0
  //   ,4,0,0,0,e,11,1,d,15,15,e,0,0,0,e,11,11,11,1f,11,11,0,0,0,1e,11,11
  //   ,1e,11,11,1e,0,0,0,e,11,10,10,10,11,e,0,0,0,1c,12,11,11,11,12
  //   ,1c,0,0,0,1f,10,10,1e,10,10,1f,0,0,0,1f,10,10,1e,10,10,10,0,0,0
  //   ,e,11,10,17,11,11,f,0,0,0,11,11,11,1f,11,11,11,0,0,0,e,5*4,e,0,0,0
  //   ,7,4*2,12,c,0,0,0,11,12,14,18,14,12,11,0,0,0,6*10,1f,0,0,0,11
  //   ,1b,15,15,11,11,11,0,0,0,11,11,19,15,13,11,11,0,0,0,e,5*11,e,0,0,0
  //   ,1e,11,11,1e,10,10,10,0,0,0,e,11,11,11,15,12,d,0,0,0,1e,11,11
  //   ,1e,14,12,11,0,0,0,f,10,10,e,1,1,1e,0,0,0,1f,6*4,0,0,0,6*11,e
  //   ,0,0,0,5*11,a,4,0,0,0,11,11,11,15,15,15,a,0,0,0,11,11,a,4,a,11,11
  //   ,0,0,0,11,11,11,a,4,4,4,0,0,0,1f,1,2,4,8,10,1f,0,0,0,1c,5*10,1c
  //   ,0,0,0,11,a,1f,4,1f,4,4,0,0,0,e,5*2,e,0,0,0,4,a,11,13*0,1f,0,0,0
  //   ,8,4,2,9*0,e,1,f,11,f,0,0,0,10,10,16,19,11,11,1e,5*0,e,10,10,11
  //   ,e,0,0,0,1,1,d,13,11,11,f,5*0,e,11,1f,10,e,0,0,0,6,9,8,1c,8,8,8
  //   ,4*0,f,11,11,f,1,e,0,0,0,10,10,16,19,11,11,11,0,0,0,4,0,c,4,4,4
  //   ,e,0,0,0,2,0,6,2,2,12,c,0,0,0,10,10,12,14,18,14,12,0,0,0,c,5*4
  //   ,e,5*0,1a,15,15,11,11,5*0,16,19,11,11,11,5*0,e,11,11,11,e,5*0
  //   ,1e,11,1e,10,10,5*0,d,13,f,1,1,5*0,16,19,10,10,10,5*0,e,10,e,1
  //   ,1e,0,0,0,8,8,1c,8,8,9,6,5*0,11,11,11,13,d,5*0,11,11,11,a,4,5*0
  //   ,11,15,15,15,a,5*0,11,a,4,a,11,5*0,11,11,f,1,e,5*0,1f,2,4,8,1f
  //   ,0,0,0,2,4,4,8,4,4,2,0,0,0,7*4,0,0,0,8,4,4,2,4,4,8,4*0,4,2,1f
  //   ,2,4,5*0,4,8,1f,8,4,338*0,1c,14,1c,0,0,0,7,4,4,4,9*0,4,4,4,1c
  //   ,7*0,10,8,4,6*0,c,c,6*0,1f,1,1f,1,2,4,5*0,1f,1,6,4,8,5*0,2,4,c
  //   ,14,4,5*0,4,1f,11,1,6,5*0,1f,4,4,4,1f,5*0,2,1f,6,a,12,5*0,8,1f
  //   ,9,a,8,6*0,e,2,2,1f,5*0,1e,2,1e,2,1e,6*0,15,15,1,6,6*0,1f,6*0
  //   ,1f,1,5,6,4,4,8,0,0,0,1,2,4,c,14,4,4,0,0,0,4,1f,11,11,1,2,4,4*0
  //   ,1f,4*4,1f,0,0,0,2,1f,2,6,a,12,2,0,0,0,8,1f,4*9,12,0,0,0,4,1f
  //   ,4,1f,4,4,4,4*0,f,9,11,1,2,c,0,0,0,8,f,12,2,2,2,4,4*0,1f,4*1,1f
  //   ,0,0,0,a,1f,a,a,2,4,8,4*0,18,1,19,1,2,1c,4*0,1f,1,2,4,a,11,0,0,0
  //   ,8,1f,9,a,8,8,7,4*0,11,11,9,1,2,c,4*0,f,9,15,3,2,c,0,0,0,2,1c
  //   ,4,1f,4,4,8,4*0,15,15,15,1,2,4,0,0,0,e,0,1f,4,4,4,8,0,0,0,8,8,8
  //   ,c,a,8,8,0,0,0,4,4,1f,4,4,8,10,4*0,e,4*0,1f,4*0,1f,1,a,4,a,10
  //   ,0,0,0,4,1f,2,4,e,15,4,0,0,0,5*2,4,8,4*0,4,2,4*11,0,0,0,10,10
  //   ,1f,10,10,10,f,4*0,1f,1,1,1,2,c
endmodule
