// Digital circuit shift_reg.dig as structural Verilog
module shift_reg (
  input  SCLK,
  input  SIN,
  input  EN,
  output [7:0] Q,
  output OF
);

  wire and_1_out;

  and and_1 (and_1_out, SCLK, EN);
  Register #(.Bits(8)) register_1 (.D({Q[6:0], SIN}), .C(and_1_out), .en(1'b1), .Q(Q));
  D_FF d_ff_1 (.D(Q[7]), .C(and_1_out), .Q(OF));  // open: nQ
endmodule

/* Test case 8 bits:
SIN SCLK Q OF
1   C    X X
0   C    X X
1   C    X X
0   C    X X
0   C    X X
1   C    X X
1   C    X X
0   C    0xa6 X
0   C    X    1
0   C    X    0
*/
