// Digital circuit spicomp.dig as structural Verilog
module spicomp (
  input  RST,
  input  CLK
);

  wire and_1_out, bitselector_1_out, comparator_1_eq, multiplexer_1_out, multiplexer_2_out, not_1_out,
       not_2_out, not_3_out, notconnected_1_out, serial_rom_1_so, X_q7, Y_q7, Z_q7;
  wire [5:0] counter_1_out;
  wire [7:0] counterpreset_1_out, IR_q, PROG_q, X_q, Y_q, Z_q;
  wire [19:0] serial_rom_1_rom_addr;

  not not_1 (not_1_out, RST);
  Counter #(.Bits(6)) counter_1 (.en(1'b1), .C(CLK), .clr(not_1_out), .out(counter_1_out));  // open: ovf
  // Probe bit on counter_1_out[2:0]
  // Probe byte on counter_1_out[5:3]
  // NotConnected on notconnected_1_out
  Multiplexer multiplexer_1 (.sel(1'b0), .in_0(X_q7), .in_1(notconnected_1_out), .out(multiplexer_1_out));
  shift_reg X (.DS7(1'b0), .SCLK(CLK), .RST(RST), .DS0(Y_q7), .S1(1'b0), .S0(1'b1), .Q(X_q), .Q7(X_q7));  // open: Q0
  shift_reg Y (.DS7(1'b0), .SCLK(CLK), .RST(RST), .DS0(Z_q7), .S1(1'b0), .S0(1'b1), .Q(Y_q), .Q7(Y_q7));  // open: Q0
  shift_reg Z (
    .DS7(1'b0), .SCLK(CLK), .RST(RST), .DS0(multiplexer_1_out), .S1(1'b0), .S0(1'b1), .Q(Z_q), .Q7(Z_q7));  // open: Q0
  BitSelector #(.Selector_Bits(3)) bitselector_1 (.in(8'h3), .sel(counter_1_out[2:0]), .out(bitselector_1_out));
  // Probe on X_q
  // Probe on Y_q
  // Probe on Z_q
  Multiplexer #(.Selector_Bits(3)) multiplexer_2 (
    .sel(counter_1_out[5:3]), .in_0(bitselector_1_out), .in_1(X_q7), .in_2(X_q7), .in_3(X_q7), .in_4(1'b0),
    .in_5(1'b0), .in_6(1'b0), .in_7(1'b0), .out(multiplexer_2_out));
  Comparator #(.Bits(3)) comparator_1 (.a(3'b000), .b(counter_1_out[2:0]), .eq(comparator_1_eq));  // open: gt, lt
  not not_2 (not_2_out, RST);
  not not_3 (not_3_out, CLK);
  serial_rom serial_rom_1 (
    .SCLK(CLK), .SI(multiplexer_2_out), .CE(not_2_out), .HOLD(1'b1), .ROM_D(PROG_q), .SO(serial_rom_1_so),
    .ROM_ADDR(serial_rom_1_rom_addr));  // open: TEST, bit, byte
  RAMAsync #(.AddrBits(20), .Bits(8)) PROG (.A(serial_rom_1_rom_addr), .D({8{1'b0}}), .we(1'b0), .Q(PROG_q));
  and and_1 (and_1_out, comparator_1_eq, not_3_out);
  // Probe PROG_DATA on PROG_q
  // Probe PROG_ADDR on serial_rom_1_rom_addr
  shift_reg IR (
    .DS7(1'b0), .SCLK(CLK), .RST(RST), .DS0(serial_rom_1_so), .S1(1'b0), .S0(1'b1), .Q(IR_q));  // open: Q0, Q7
  CounterPreset #(.Bits(8)) counterpreset_1 (
    .en(1'b1), .C(and_1_out), .dir(1'b1), .in(IR_q), .ld(1'b1), .clr(not_2_out), .out(counterpreset_1_out));  // open: ovf
  // Probe IR_SR on IR_q
  // Probe IR on counterpreset_1_out
endmodule

/* Test case boot:
           RST_ CLK IR
	   0    0   0
loop(n,32)
           1    0   X
           1    1   X
end loop
loop(n,8)
           1    0   X
           1    1   X
end loop
           1    0   0xAB
loop(n,7)
           1    C   0xAB
end loop
           1    0   0xAB
           1    1   0xAB
           1    0   0xCD
memory PROG(0x0)=0xAB;
memory PROG(0x1)=0xCD;
*/
