// Digital circuit lutcomp.dig as structural Verilog
module lutcomp (
  input  RESET,
  input  clk,
  output HALT
);

  wire and_2_out, CLK_t, CLK_t_t, comparator_1_eq, counter_1_ovf, decoder_1_out_0, decoder_1_out_1,
       decoder_1_out_2, decoder_1_out_3, decoder_1_out_4, decoder_1_out_5, decoder_1_out_6, decoder_1_out_7,
       io_1_key_clk, io_1_term_clk, keyboard_1_av, not_2_out, switch_1_b, uc_1_p4, uc_1_p6, uc_1_p7, uc_1_p8,
       uc_1_p9, uc_1_p10, uc_1_p11, uc_1_p12, uc_1_p13, uc_1_p14, uc_1_p15, uc_1_p16, uc_1_p17, uc_1_p18,
       uc_1_p20, uc_1_p21, uc_1_p22, uc_1_p23, undriven, undriven_2, undriven_4, undriven_5, undriven_9,
       undriven_10, undriven_11, undriven_12, undriven_13;
  wire [1:0] io_1_in_source;
  wire [2:0] uc_1_p5;
  wire [3:0] undriven_8;
  wire [6:0] undriven_6;
  wire [7:0] counter_3_out, io_1_in_value, uc_1_p3, undriven_7;
  wire [15:0] counter_2_out, keyboard_1_d;
  wire [18:0] counter_1_out;
  wire [23:0] pc_1_pc, undriven_3;

  and and_1 (CLK_t, clk, HALT);
  Stop stop_1 (.stop(~HALT));
  not not_1 (CLK_t_t, CLK_t);
  // Probe on counter_1_out
  Counter #(.Bits(19)) counter_1 (.en(1'b1), .C(CLK_t), .clr(1'b0), .out(counter_1_out), .ovf(counter_1_ovf));
  Break #(.Cycles(20000000)) break_1 (.brk(counter_1_ovf));
  // uc uc_1: pin names not known; wires that end beside it: CLK_t_t, RESET, uc_1_p3, uc_1_p4, uc_1_p5, uc_1_p6, uc_1_p7, uc_1_p8, uc_1_p9, uc_1_p10, uc_1_p11, uc_1_p12, uc_1_p13, uc_1_p14, uc_1_p15, uc_1_p16, uc_1_p17, uc_1_p18, HALT, uc_1_p20, uc_1_p21, uc_1_p22, uc_1_p23
  not not_2 (not_2_out, uc_1_p4);
  // Probe on undriven_9
  // Probe on undriven_10
  // Probe on undriven_11
  // Probe on undriven_12
  // Probe on undriven_13
  and and_2 (and_2_out, uc_1_p6, ~uc_1_p23);  // And
  Switch switch_1 (.A(uc_1_p6), .B(switch_1_b));
  pc pc_1 (.PC_INC(uc_1_p6), .RESET(RESET), .PC_SPE(uc_1_p23), .OE(not_2_out), .ADDR(undriven_3), .PC(pc_1_pc));
  // Probe $uPC on {undriven_8, undriven_7, undriven_6}
  // Probe on undriven_6
  // Probe $IR0 on undriven_7
  // Probe $FLAGS on undriven_8
  Counter #(.Bits(16)) counter_2 (.en(1'b1), .C(uc_1_p6), .clr(1'b0), .out(counter_2_out));  // open: ovf
  Break #(.Cycles(10000000)) break_2 (.brk(switch_1_b));
  PullDown pulldown_1 (.out(switch_1_b));
  Counter #(.Bits(8)) counter_3 (.en(1'b1), .C(and_2_out), .clr(1'b0), .out(counter_3_out));  // open: ovf
  // Probe PC on pc_1_pc
  io io_1 (
    .DATA(uc_1_p3), .TTYIN_CP(uc_1_p10), .TTYIN_OE(uc_1_p22), .TTYOUT_CP(uc_1_p18), .KEY_D(keyboard_1_d),
    .KEY_AV(keyboard_1_av), .TERM_CLK(io_1_term_clk), .KEY_CLK(io_1_key_clk), .IN_SOURCE(io_1_in_source),
    .IN_VALUE(io_1_in_value));
  RAMDualPort #(.AddrBits(16), .Bits(24)) PC_LOG (
    .A(counter_2_out), .Din(pc_1_pc), .str(1'b1), .C(uc_1_p6), .ld(1'b0));  // open: D
  RAMDualPort #(.AddrBits(8), .Bits(24)) JMP_LOG (
    .A(counter_3_out), .Din(pc_1_pc), .str(1'b1), .C(and_2_out), .ld(1'b0));  // open: D
  Keyboard keyboard_1 (.C(io_1_key_clk), .en(1'b1), .D(keyboard_1_d), .av(keyboard_1_av));
  Terminal terminal_1 (.D(uc_1_p3), .C(io_1_term_clk), .en(1'b1));
  Comparator #(.Bits(24)) comparator_1 (.a(pc_1_pc), .b(24'hffff), .eq(comparator_1_eq));  // open: gt, lt
  Break break_3 (.brk(comparator_1_eq));
  memory memory_1 (
    .MEM_CP(uc_1_p9), .ADDR_OE(uc_1_p4), .A0_CP(uc_1_p15), .A1_CP(uc_1_p16), .A2_CP(uc_1_p17),
    .MEM_OE(uc_1_p21), .DATA(uc_1_p3), .ADDR(undriven_3));
  \reg  W (.OE(undriven), .CP(uc_1_p11), .DATA(uc_1_p3));  // open: IO
  \reg  X (.OE(undriven_2), .CP(uc_1_p12), .DATA(uc_1_p3));  // open: IO
  \reg  Y (.OE(undriven_4), .CP(uc_1_p13), .DATA(uc_1_p3));  // open: IO
  \reg  Z (.OE(undriven_5), .CP(uc_1_p14), .DATA(uc_1_p3));  // open: IO
  // Probe on io_1_in_source
  // Probe on io_1_in_value
  // Probe ADDR on undriven_3
  // Probe DATA on uc_1_p3
  Decoder #(.Selector_Bits(3)) decoder_1 (
    .sel(uc_1_p5), .out_0(decoder_1_out_0), .out_1(decoder_1_out_1), .out_2(decoder_1_out_2),
    .out_3(decoder_1_out_3), .out_4(decoder_1_out_4), .out_5(decoder_1_out_5), .out_6(decoder_1_out_6),
    .out_7(decoder_1_out_7));
  alu alu_1 (
    .ALU_OP(uc_1_p5), .ALU_OE(uc_1_p20), .ALU_CP(uc_1_p8), .IN1_CP(uc_1_p7), .DATA(uc_1_p3));  // open: IN1, ALU_REG, ALU_RESULT
  // Probe AddLo on decoder_1_out_0
  // Probe AddHiNC on decoder_1_out_2
  // Probe Or on decoder_1_out_4
  // Probe And on decoder_1_out_6
  // Probe MulHi on decoder_1_out_1
  // Probe AddHiC on decoder_1_out_3
  // Probe Div on decoder_1_out_5
  // Probe Special on decoder_1_out_7

  // Notes on the sheet:
  //   RESET: default 1
  //   clk: Hz: 1000000
  //   4A
  //   4B
  //   4Y
  //   6A
  //   6Y
  //   3A
  //   3Y
endmodule

/* Test case:
RESET_ HALT
0      1
*/
