// Digital circuit ps2.dig as structural Verilog
module ps2 (
  input  TTYIN_CP,
  input  CLK,
  input  [7:0] DATA,
  input  TTYIN_OE
);

  wire _74161_1_pin9, _74161_1_pin15, _74299_1_pin18, and_1_out, not_1_out, not_2_out, paralleltops2_1_ack,
       PS2_CLK, PS2_DATA;
  wire [3:0] _74161_1_pin3, _74161_1_pin14;
  wire [5:0] _74299_1_pin5;
  wire [6:5] _74299_2_pin4;
  wire [7:0] counter_1_out;

  Counter #(.Bits(8)) counter_1 (.en(1'b1), .C(paralleltops2_1_ack), .clr(1'b0), .out(counter_1_out));  // open: ovf
  ParallelToPS2 paralleltops2_1 (
    .CLK(CLK), .DATA(counter_1_out), .PS2_CLK(PS2_CLK), .PS2_DATA(PS2_DATA), .ACK(paralleltops2_1_ack));
  // Probe PS2_CLK on PS2_CLK
  // Probe PS2_DATA on PS2_DATA
  PullUp pullup_1 (.out(PS2_CLK));
  PullUp pullup_2 (.out(PS2_DATA));
  not not_1 (not_1_out, TTYIN_CP);
  and and_1 (and_1_out, not_1_out, not_2_out);
  not not_2 (not_2_out, PS2_CLK);
  _74161 _74161_1 (
    .pin1(1'b1), .pin2(and_1_out), .pin3(_74161_1_pin3[0]), .pin4(_74161_1_pin3[1]), .pin5(_74161_1_pin3[2]),
    .pin6(_74161_1_pin3[3]), .pin7(1'b1), .pin8(1'b0), .pin9(_74161_1_pin9), .pin10(1'b1),
    .pin11(_74161_1_pin14[3]), .pin12(_74161_1_pin14[2]), .pin13(_74161_1_pin14[1]),
    .pin14(_74161_1_pin14[0]), .pin15(_74161_1_pin15), .pin16(1'b1));
  // Probe PS2_ROF on _74161_1_pin15
  // Probe PS2_RECVBIT on _74161_1_pin14
  not not_3 (_74161_1_pin9, _74161_1_pin15);
  _74299 _74299_1 (
    .pin1(1'b0), .pin2(TTYIN_OE), .pin3(1'b0), .pin4(DATA[0]), .pin5(_74299_1_pin5[4]),
    .pin6(_74299_1_pin5[2]), .pin7(_74299_1_pin5[0]), .pin9(not_1_out), .pin10(1'b0), .pin11(1'b1),
    .pin12(not_2_out), .pin13(_74299_1_pin5[1]), .pin14(_74299_1_pin5[3]), .pin15(_74299_1_pin5[5]),
    .pin16(DATA[1]), .pin18(_74299_1_pin18), .pin19(1'b1), .pin20(1'b1));  // open: pin8, pin17
  _74299 _74299_2 (
    .pin1(1'b0), .pin2(TTYIN_OE), .pin3(1'b0), .pin4(_74299_2_pin4[6]), .pin5(DATA[6]), .pin6(DATA[4]),
    .pin7(DATA[2]), .pin8(_74299_1_pin18), .pin9(not_1_out), .pin10(1'b0), .pin11(1'b1), .pin12(not_2_out),
    .pin13(DATA[3]), .pin14(DATA[5]), .pin15(_74299_2_pin4[5]), .pin16(DATA[7]), .pin18(PS2_DATA),
    .pin19(1'b1), .pin20(1'b1));  // open: pin17
  // Probe PS2_INCOMING on {DATA[7], _74299_2_pin4, DATA[6:0], _74299_1_pin5}
  // Probe PS2_START on _74299_1_pin5[5]
  // Probe PS2_BYTE on {_74299_2_pin4[5], DATA[6:0]}
  // Probe PS2_PARITY on _74299_2_pin4[6]
  // Probe PS2_STOP on DATA[7]
  assign PS2_CLK = _74161_1_pin15 ? 1'b0 : 1'bz;  // Driver driver_1
  // Probe PS2_READY on _74161_1_pin15
  // also tied to GND on the sheet: {_74161_1_pin3[0], _74161_1_pin3[1], _74161_1_pin3[3]}
  // also tied to VCC on the sheet: _74161_1_pin3[2]

  // Notes on the sheet:
  //   TTYIN_OE: default 1
endmodule

/* Test case e2e:
            CLK PS2_CLK TTYIN_CP PS2_READY TTYIN_OE_ DATA_out
            C   1       0        0         1         Z
repeat(100) C   X       0        X         1         Z
repeat(100) C   0       0        1         1         Z
repeat(100) C   0       0        1         1         Z
loop(a,300)
            C   1       C        0         1         Z
            C   1       0        0         1         Z
repeat(40)  C   X       0        X         1         Z
repeat(40)  C   0       0        1         0         (0x80|(a+2))
end loop
*/
